# Fritzing sketch blinds_controller (saved by Fritzing 0.9.5d)
circuit board: 8.46667cm x 5.64444cm
breadboards: 1

parts:
  Nano = Arduino Nano (Rev3.0)
  BTN_1 = Pushbutton [package="[THT]"]
  R2 = Resistor [tolerance=±5% resistance=1k package=THT]
  Stepper_Driver = Header 6 [package=1x06_smd_straight_alt]
  PhotoCell = Header 2 [package=jst-2-pth]
  BTN_2 = Pushbutton [package="[THT]"]

nets:
  N1: Nano.GND, BTN_1.Pin_1, BTN_1.Pin_2, R2.Pin_1, Stepper_Driver.5, BTN_2.Pin_1, BTN_2.Pin_2
  N2: Nano.D2, BTN_2.Pin_3, BTN_2.Pin_4
  N3: Nano.D3, BTN_1.Pin_3, BTN_1.Pin_4
  N4: Nano.D8, Stepper_Driver.4
  N5: Nano.D9, Stepper_Driver.3
  N6: Nano.D10, Stepper_Driver.2
  N7: Nano.D11/MOSI, Stepper_Driver.1
  N8: Nano.5V, Stepper_Driver.6, PhotoCell.1
  N9: Nano.A2, R2.Pin_0, PhotoCell.2
